# Fritzing sketch Photon2_LED_LDR (saved by Fritzing 0.9.3b)
circuit board: 5.13238cm x 3.33763cm
breadboards: 1

parts:
  LED = LED - 3mm [color="Blue (470nm)" package="3 mm [THT]"]
  R2 = Resistor [tolerance=±5% resistance=220 package=THT]
  Photon2 = photon2 [part_number=Photon2]
  R3 = Resistor [tolerance=±5% resistance=10k package=THT]
  LDR = Photocell (LDR) [package=THT]

nets:
  N1: LED.cathode, R2.Pin_1
  N2: LED.anode, Photon2.Pin_11
  N3: R2.Pin_0, Photon2.Pin_4, Photon2.Pin_30, R3.Pin_0
  N4: Photon2.Pin_2, LDR.pin_0
  N5: Photon2.Pin_6, R3.Pin_1, LDR.pin_1
  N6: Photon2.Pin_28, Photon2.Pin_29

custom parts:
  photon2: The Photon 2 is a development module with a microcontroller and Wi-Fi networking.
